# Fritzing sketch LedControlV3 (saved by Fritzing 0.9.4)
circuit board: 4.34006cm x 4.29436cm
breadboards: 1

parts:
  Q1 = npn-Powertransistor [package="TO220 [THT]"]
  Q2 = npn-Powertransistor [package="TO220 [THT]"]
  Q3 = npn-Powertransistor [package="TO220 [THT]"]
  Q4 = npn-Powertransistor [package="TO220 [THT]"]
  Power_plug1 = Power plug
  1_2_3_4_gnd = female pin header, 5 pins [form="♀ (female)"]
  R1 = Resistor [tolerance=±5% resistance=220 package=THT]
  R2 = Resistor [tolerance=±5% resistance=220 package=THT]
  R3 = Resistor [tolerance=±5% resistance=220 package=THT]
  R4 = Resistor [tolerance=±5% resistance=220 package=THT]
  J1 = female pin header, 3 pins [form="♀ (female)"]
  J2 = female pin header, 3 pins [form="♀ (female)"]
  J3 = female pin header, 3 pins [form="♀ (female)"]
  J4 = female pin header, 3 pins [form="♀ (female)"]
  V+_R_G_B1 = female pin header, 5 pins [form="♀ (female)"]
  J5 = Camdenboss CTB0158-5 [part_number=CTB0158-5 package=THT]
  V+_R_G_B_W = rounded female pin header, 5 pins [form="♀ (female rounded)"]

nets:
  N1: Q1.base, R3.Pin_1, J4.pin3
  N2: Q1.collector, V+_R_G_B1.pin4, J5.pin4, V+_R_G_B_W.pin4
  N3: Q1.emitter, Q2.emitter, Q3.emitter, Q4.emitter, Power_plug1.GND, 1_2_3_4_gnd.pin5, J1.pin1, J2.pin1, J3.pin1, J4.pin1
  N4: Q2.base, R4.Pin_1, J3.pin3
  N5: Q2.collector, V+_R_G_B1.pin3, J5.pin3, V+_R_G_B_W.pin3
  N6: Q3.base, R2.Pin_1, J2.pin3
  N7: Q3.collector, V+_R_G_B1.pin2, J5.pin2, V+_R_G_B_W.pin2
  N8: Q4.base, R1.Pin_1, J1.pin3
  N9: Q4.collector, V+_R_G_B1.pin1, J5.pin1, V+_R_G_B_W.pin1
  N10: Power_plug1.VCC, V+_R_G_B1.pin5, J5.pin5, V+_R_G_B_W.pin5
  N11: 1_2_3_4_gnd.pin1, R1.Pin_0, J1.pin2
  N12: 1_2_3_4_gnd.pin2, R2.Pin_0, J2.pin2
  N13: 1_2_3_4_gnd.pin3, R4.Pin_0, J3.pin2
  N14: 1_2_3_4_gnd.pin4, R3.Pin_0, J4.pin2

notes:
  LEDControlv0.3
