# Fritzing sketch Remote Zone (saved by Fritzing 0.9.4)
circuit board: 8.37717cm x 8.06863cm
breadboards: 2

parts:
  DC_to_DC = RioRand LM2596
  NodeMcu_ESP12E = ESP8266 NodeMCU LoLin module
  Power_plug1 = Power plug
  Q1 = npn-Powertransistor [package="TO220 [THT]"]
  Q2 = npn-Powertransistor [package="TO220 [THT]"]
  Q3 = npn-Powertransistor [package="TO220 [THT]"]
  Q4 = npn-Powertransistor [package="TO220 [THT]"]
  J1 = female pin header, 16 pins [form="♀ (female)"]
  J2 = female pin header, 16 pins [form="♀ (female)"]
  J4 = female pin header, 3 pins [form="♀ (female)"]
  J5 = female pin header, 3 pins [form="♀ (female)"]
  R1 = Resistor [tolerance=±5% resistance=220 package=THT]
  R2 = Resistor [tolerance=±5% resistance=220 package=THT]
  R3 = Resistor [tolerance=±5% resistance=220 package=THT]
  R4 = Resistor [tolerance=±5% resistance=220 package=THT]
  R5 = Resistor [tolerance=±5% resistance=220 package=THT]
  Q6 = npn-Powertransistor [package="TO220 [THT]"]
  R6 = Resistor [tolerance=±5% resistance=220 package=THT]
  J7 = female pin header, 6 pins [form="♀ (female)"]
  J6 = female pin header, 6 pins [form="♀ (female)"]
  J8 = female pin header, 2 pins [form="♀ (female)"]
  J9 = female pin header, 2 pins [form="♀ (female)"]
  Q5 = npn-Powertransistor [package="TO220 [THT]"]
  J10 = screw terminal, 8 pins
  J11 = female pin header, 15 pins [form="♀ (female)"]

nets:
  N1: DC_to_DC.Pin_1, Power_plug1.VCC, J5.pin1, J5.pin2, J5.pin3, J8.pin1, J8.pin2, J9.pin1, J9.pin2, J10.pin1, J10.pin8
  GND: DC_to_DC.Pin_2, DC_to_DC.Pin_4, NodeMcu_ESP12E.GND, Power_plug1.GND, Q1.emitter, Q2.emitter, Q3.emitter, Q4.emitter, J1.pin7, J1.pin14, J2.pin7, J2.pin14, J4.pin1, J4.pin2, J4.pin3, Q6.emitter, Q5.emitter, J11.pin2, J11.pin10, J11.pin14
  N2: DC_to_DC.Pin_3, NodeMcu_ESP12E.Vin, J11.pin15
  N3: NodeMcu_ESP12E.D0, J1.pin1, R1.Pin_1
  N4: NodeMcu_ESP12E.D1, J1.pin2, R2.Pin_1
  N5: NodeMcu_ESP12E.D2, J1.pin3, R3.Pin_1
  N6: NodeMcu_ESP12E.D3, J1.pin4, R4.Pin_1
  N7: NodeMcu_ESP12E.D4, J1.pin5, R5.Pin_1
  N8: NodeMcu_ESP12E.3V3, J1.pin6, J1.pin15, J2.pin6, J2.pin15, J11.pin11
  N9: NodeMcu_ESP12E.D5, J1.pin8, R6.Pin_1
  N10: NodeMcu_ESP12E.D6, J1.pin9, J2.pin9
  N11: NodeMcu_ESP12E.D7, J1.pin10, J2.pin10
  N12: NodeMcu_ESP12E.D8, J1.pin11, J2.pin11
  N13: NodeMcu_ESP12E.RX, J1.pin12, J2.pin12
  N14: NodeMcu_ESP12E.TX, J1.pin13, J2.pin13
  N15: NodeMcu_ESP12E.RST, J11.pin13
  N16: NodeMcu_ESP12E.EN, J11.pin12
  N17: NodeMcu_ESP12E.SK, J11.pin9
  N18: NodeMcu_ESP12E.S0, J11.pin8
  N19: NodeMcu_ESP12E.SC, J11.pin7
  N20: NodeMcu_ESP12E.S1, J11.pin6
  N21: NodeMcu_ESP12E.S2, J11.pin5
  N22: NodeMcu_ESP12E.S3, J11.pin4
  N23: NodeMcu_ESP12E.VU, J11.pin3
  N24: NodeMcu_ESP12E.A0, J11.pin1
  N25: Q1.base, J2.pin1, R1.Pin_0
  N26: Q1.collector, J7.pin1, J6.pin1, J10.pin2
  N27: Q2.base, Q2.collector, J2.pin2, R2.Pin_0, J7.pin2, J6.pin2, J10.pin3
  N28: Q3.base, J2.pin3, R3.Pin_0
  N29: Q3.collector, J7.pin3, J6.pin3, J10.pin4
  N30: Q4.base, J2.pin5, R5.Pin_0
  N31: Q4.collector, J7.pin5, J6.pin5, J10.pin6
  N32: J1.pin16, J2.pin16
  N33: J2.pin4, R4.Pin_0, Q5.base
  N34: J2.pin8, Q6.base, R6.Pin_0
  N35: Q6.collector, J7.pin6, J6.pin6, J10.pin7
  N36: J7.pin4, J6.pin4, Q5.collector, J10.pin5

notes:
  Duxman Luces v.0.4
  Remote Zone V0.1

custom parts:
  ESP8266 NodeMCU LoLin module: ESP8266 based NodeMCU
